// Logisim project 4B_q3.circ as structural Verilog: 2 circuits, main circuit main
module main (
  input  Reset,
  input  Load,
  output out_3,
  output out_4,
  output out_5,
  output out_6,
  output out_7,
  output out_8,
  output out_9,
  output out_10
);

  wire clock_1_out, or_1_out;
  wire [7:0] adder_1_out, and_1_out, register_1_q;

  or or_1 (or_1_out, Reset, and_1_out[3]);
  Register register_1 (.D(adder_1_out), .Q(register_1_q), .clk(clock_1_out), .clr(or_1_out));  // open: en
  Adder adder_1 (.a(8'h1), .b(register_1_q), .out(adder_1_out));  // open: cin, cout
  assign and_1_out = register_1_q & 8'h8;  // AND_Gate and_1, 8 bits wide
  Clock clock_1 (.out(clock_1_out));
  RAM ram_1 (
    .addr(register_1_q), .data({out_3, out_7, out_4, out_8, out_5, out_9, out_6, out_10}), .sel(1'b1),
    .clk(clock_1_out), .ld(Load), .clr(Reset));
endmodule

module StudentNumber (
  input  a,
  input  b,
  input  c,
  input  d,
  input  e,
  input  f,
  input  g,
  input  h,
  output x,
  output y,
  output z,
  output u,
  output v,
  output w,
  output s,
  output t
);

  wire and_2_out, and_3_out, and_4_out, and_5_out, and_6_out, and_7_out, and_8_out, not_1_out, not_2_out,
       not_3_out, not_4_out, not_5_out, not_6_out, not_7_out, not_8_out, not_9_out, not_10_out;

  and and_1 (v, f, g, not_1_out);
  not not_1 (not_1_out, h);
  not not_2 (not_2_out, f);
  and and_2 (and_2_out, not_2_out, g, not_3_out);
  not not_3 (not_3_out, h);
  and and_3 (and_3_out, f, not_4_out);
  not not_4 (not_4_out, g);
  not not_5 (not_5_out, f);
  and and_4 (and_4_out, not_5_out, h);
  and and_5 (and_5_out, g, h);
  and and_6 (and_6_out, f, not_6_out, not_7_out);
  not not_6 (not_6_out, g);
  not not_7 (not_7_out, h);
  not not_8 (not_8_out, g);
  not not_9 (not_9_out, f);
  and and_7 (and_7_out, not_9_out, h);
  and and_8 (and_8_out, f, not_10_out);
  not not_10 (not_10_out, h);
  or or_1 (w, and_2_out, and_3_out);
  or or_2 (s, and_4_out, and_5_out, and_6_out);
  or or_3 (t, not_8_out, and_7_out, and_8_out);

  assign u = 1'b0;
  assign x = 1'b0;
  assign y = 1'b0;
  assign z = 1'b0;
endmodule
