// Logisim project GROUP30-ASS5.circ as structural Verilog
module ALU (
  input  a7,
  input  a6,
  input  a5,
  input  a4,
  input  a3,
  input  a2,
  input  a1,
  input  a0,
  input  b7,
  input  b6,
  input  b5,
  input  b4,
  input  b3,
  input  b2,
  input  b1,
  input  b0,
  input  Bit_0,
  input  Bit_1
);

  wire bit_wise_and_1_out_17, bit_wise_and_1_out_18, bit_wise_and_1_out_19, bit_wise_and_1_out_20,
       bit_wise_and_1_out_21, bit_wise_and_1_out_22, bit_wise_and_1_out_23, bit_wise_and_1_out_24,
       control_1_out_10, control_1_out_11, control_1_out_12, control_1_out_13, control_1_out_14,
       control_1_out_15, control_1_out_16, control_1_out_17, control_2_out_10, control_2_out_11,
       control_2_out_12, control_2_out_13, control_2_out_14, control_2_out_15, control_2_out_16,
       control_2_out_17, control_3_out_10, control_3_out_11, control_3_out_12, control_3_out_13,
       control_3_out_14, control_3_out_15, control_3_out_16, control_3_out_17, n2bit_control_1_x,
       n2bit_control_1_y, n2bit_control_1_z, n8_bit_adder_1_o0, n8_bit_adder_1_o1, n8_bit_adder_1_o2,
       n8_bit_adder_1_o3, n8_bit_adder_1_o4, n8_bit_adder_1_o5, n8_bit_adder_1_o6, n8_bit_adder_1_o7,
       n8_bit_subtractor_1_out_17, n8_bit_subtractor_1_out_18, n8_bit_subtractor_1_out_19,
       n8_bit_subtractor_1_out_20, n8_bit_subtractor_1_out_21, n8_bit_subtractor_1_out_22,
       n8_bit_subtractor_1_out_23, n8_bit_subtractor_1_out_24, or_1_out, or_2_out, or_3_out, or_4_out,
       or_5_out, or_6_out, or_7_out, or_8_out;

  _8_bit_adder u_8_bit_adder_1 (
    .a7(a7), .b7(b7), .a6(a6), .b6(b6), .a5(a5), .b5(b5), .a4(a4), .b4(b4), .a3(a3), .b3(b3), .a2(a2),
    .b2(b2), .a1(a1), .b1(b1), .a0(a0), .b0(b0), .o7(n8_bit_adder_1_o7), .o6(n8_bit_adder_1_o6),
    .o5(n8_bit_adder_1_o5), .o4(n8_bit_adder_1_o4), .o3(n8_bit_adder_1_o3), .o2(n8_bit_adder_1_o2),
    .o1(n8_bit_adder_1_o1), .o0(n8_bit_adder_1_o0));  // open: o8
  _2bit_control u_2bit_control_1 (
    .a(Bit_1), .b(Bit_0), .x(n2bit_control_1_x), .y(n2bit_control_1_y), .z(n2bit_control_1_z));
  control control_1 (
    .Control(n2bit_control_1_z), .a7(n8_bit_adder_1_o7), .a6(n8_bit_adder_1_o6), .a5(n8_bit_adder_1_o5),
    .a4(n8_bit_adder_1_o4), .a3(n8_bit_adder_1_o3), .a2(n8_bit_adder_1_o2), .a1(n8_bit_adder_1_o1),
    .a0(n8_bit_adder_1_o0), .out_10(control_1_out_10), .out_11(control_1_out_11), .out_12(control_1_out_12),
    .out_13(control_1_out_13), .out_14(control_1_out_14), .out_15(control_1_out_15),
    .out_16(control_1_out_16), .out_17(control_1_out_17));
  or or_1 (or_1_out, control_1_out_10, control_2_out_10, control_3_out_10);
  or or_2 (or_2_out, control_1_out_11, control_2_out_11, control_3_out_11);
  LED led_1 (.in(or_1_out));
  LED led_2 (.in(or_2_out));
  or or_3 (or_3_out, control_1_out_13, control_2_out_13, control_3_out_13);
  or or_4 (or_4_out, control_1_out_12, control_2_out_12, control_3_out_12);
  LED led_3 (.in(or_3_out));
  LED led_4 (.in(or_4_out));
  or or_5 (or_5_out, control_1_out_14, control_2_out_14, control_3_out_14);
  or or_6 (or_6_out, control_1_out_15, control_2_out_15, control_3_out_15);
  LED led_5 (.in(or_6_out));
  LED led_6 (.in(or_5_out));
  or or_7 (or_7_out, control_1_out_16, control_2_out_16, control_3_out_16);
  or or_8 (or_8_out, control_1_out_17, control_2_out_17, control_3_out_17);
  LED led_7 (.in(or_8_out));
  LED led_8 (.in(or_7_out));
  _8_bit_Subtractor u_8_bit_subtractor_1 (
    .b7(b7), .a7(a7), .b6(b6), .a6(a6), .b5(b5), .a5(a5), .b4(b4), .a4(a4), .b3(b3), .a3(a3), .b2(b2),
    .a2(a2), .b1(b1), .a1(a1), .b0(b0), .a0(a0), .out_17(n8_bit_subtractor_1_out_17),
    .out_18(n8_bit_subtractor_1_out_18), .out_19(n8_bit_subtractor_1_out_19),
    .out_20(n8_bit_subtractor_1_out_20), .out_21(n8_bit_subtractor_1_out_21),
    .out_22(n8_bit_subtractor_1_out_22), .out_23(n8_bit_subtractor_1_out_23),
    .out_24(n8_bit_subtractor_1_out_24));
  control control_2 (
    .Control(n2bit_control_1_y), .a7(n8_bit_subtractor_1_out_17), .a6(n8_bit_subtractor_1_out_18),
    .a5(n8_bit_subtractor_1_out_19), .a4(n8_bit_subtractor_1_out_20), .a3(n8_bit_subtractor_1_out_21),
    .a2(n8_bit_subtractor_1_out_22), .a1(n8_bit_subtractor_1_out_23), .a0(n8_bit_subtractor_1_out_24),
    .out_10(control_2_out_10), .out_11(control_2_out_11), .out_12(control_2_out_12),
    .out_13(control_2_out_13), .out_14(control_2_out_14), .out_15(control_2_out_15),
    .out_16(control_2_out_16), .out_17(control_2_out_17));
  bit_wise_AND bit_wise_and_1 (
    .b7(a7), .a7(b7), .b6(b6), .a6(a6), .b5(b5), .a5(a5), .b4(b4), .a4(a4), .b3(b3), .a3(a3), .b2(b2),
    .a2(a2), .b1(b1), .a1(a1), .b0(b0), .a0(a0), .out_17(bit_wise_and_1_out_17),
    .out_18(bit_wise_and_1_out_18), .out_19(bit_wise_and_1_out_19), .out_20(bit_wise_and_1_out_20),
    .out_21(bit_wise_and_1_out_21), .out_22(bit_wise_and_1_out_22), .out_23(bit_wise_and_1_out_23),
    .out_24(bit_wise_and_1_out_24));
  control control_3 (
    .Control(n2bit_control_1_x), .a7(bit_wise_and_1_out_17), .a6(bit_wise_and_1_out_18),
    .a5(bit_wise_and_1_out_19), .a4(bit_wise_and_1_out_20), .a3(bit_wise_and_1_out_21),
    .a2(bit_wise_and_1_out_22), .a1(bit_wise_and_1_out_23), .a0(bit_wise_and_1_out_24),
    .out_10(control_3_out_10), .out_11(control_3_out_11), .out_12(control_3_out_12),
    .out_13(control_3_out_13), .out_14(control_3_out_14), .out_15(control_3_out_15),
    .out_16(control_3_out_16), .out_17(control_3_out_17));

  // Notes on the sheet:
  //   01 - Addition 
  //   10 - Subtraction
  //   11 - AND
  //   For subtraction: result = a - b
endmodule

module _8_bit_adder (
  input  a7,
  input  a6,
  input  a5,
  input  a4,
  input  a3,
  input  a2,
  input  a1,
  input  a0,
  input  b7,
  input  b6,
  input  b5,
  input  b4,
  input  b3,
  input  b2,
  input  b1,
  input  b0,
  output o8,
  output o7,
  output o6,
  output o5,
  output o4,
  output o3,
  output o2,
  output o1,
  output o0
);

  wire full_adder_2_c_out, full_adder_3_c_out, full_adder_4_c_out, full_adder_5_c_out, full_adder_6_c_out,
       full_adder_7_c_out, half_adder_1_carry_out;

  Full_Adder full_adder_1 (.X(b7), .Y(a7), .C_in(full_adder_2_c_out), .S(o7), .C_out(o8));
  Full_Adder full_adder_2 (.X(b6), .Y(a6), .C_in(full_adder_3_c_out), .S(o6), .C_out(full_adder_2_c_out));
  Full_Adder full_adder_3 (.X(b5), .Y(a5), .C_in(full_adder_4_c_out), .S(o5), .C_out(full_adder_3_c_out));
  Full_Adder full_adder_4 (.X(b4), .Y(a4), .C_in(full_adder_5_c_out), .S(o4), .C_out(full_adder_4_c_out));
  Full_Adder full_adder_5 (.X(b3), .Y(a3), .C_in(full_adder_6_c_out), .S(o3), .C_out(full_adder_5_c_out));
  Full_Adder full_adder_6 (.X(b2), .Y(a2), .C_in(full_adder_7_c_out), .S(o2), .C_out(full_adder_6_c_out));
  Full_Adder full_adder_7 (.X(b1), .Y(a1), .C_in(half_adder_1_carry_out), .S(o1), .C_out(full_adder_7_c_out));
  Half_Adder half_adder_1 (.A(b0), .B(a0), .S(o0), .Carry_Out(half_adder_1_carry_out));
endmodule

module Full_Adder (
  input  X,
  input  Y,
  input  C_in,
  output S,
  output C_out
);

  wire and_1_out, and_2_out, xor_1_out;

  xor xor_1 (xor_1_out, X, Y);
  xor xor_2 (S, xor_1_out, C_in);
  and and_1 (and_1_out, xor_1_out, C_in);
  and and_2 (and_2_out, X, Y);
  or or_1 (C_out, and_1_out, and_2_out);
endmodule

module Half_Adder (
  input  A,
  input  B,
  output S,
  output Carry_Out
);

  wire and_1_out, and_2_out, not_1_out, not_2_out;

  and and_1 (and_1_out, A, not_1_out);
  not not_1 (not_1_out, B);
  not not_2 (not_2_out, A);
  and and_2 (and_2_out, not_2_out, B);
  and and_3 (Carry_Out, A, B);
  or or_1 (S, and_1_out, and_2_out);
endmodule

// 8 bit subtractor
module _8_bit_Subtractor (
  input  a7,
  input  a6,
  input  a5,
  input  a4,
  input  a3,
  input  a2,
  input  a1,
  input  a0,
  input  b7,
  input  b6,
  input  b5,
  input  b4,
  input  b3,
  input  b2,
  input  b1,
  input  b0,
  output out_17,
  output out_18,
  output out_19,
  output out_20,
  output out_21,
  output out_22,
  output out_23,
  output out_24
);

  wire full_subtractor_2_carryout, full_subtractor_3_carryout, full_subtractor_4_carryout,
       full_subtractor_5_carryout, full_subtractor_6_carryout, full_subtractor_7_carryout,
       half_subtractor_1_carry_out;

  Full_Subtractor full_subtractor_1 (
    .a(a7), .b(b7), .CarryIn(full_subtractor_2_carryout), .o0(out_17));  // open: CarryOut
  Full_Subtractor full_subtractor_2 (
    .a(a6), .b(b6), .CarryIn(full_subtractor_3_carryout), .CarryOut(full_subtractor_2_carryout), .o0(out_18));
  Full_Subtractor full_subtractor_3 (
    .a(a5), .b(b5), .CarryIn(full_subtractor_5_carryout), .CarryOut(full_subtractor_3_carryout), .o0(out_19));
  Full_Subtractor full_subtractor_4 (
    .a(a3), .b(b3), .CarryIn(full_subtractor_6_carryout), .CarryOut(full_subtractor_4_carryout), .o0(out_21));
  Full_Subtractor full_subtractor_5 (
    .a(a4), .b(b4), .CarryIn(full_subtractor_4_carryout), .CarryOut(full_subtractor_5_carryout), .o0(out_20));
  Full_Subtractor full_subtractor_6 (
    .a(a2), .b(b2), .CarryIn(full_subtractor_7_carryout), .CarryOut(full_subtractor_6_carryout), .o0(out_22));
  Full_Subtractor full_subtractor_7 (
    .a(a1), .b(b1), .CarryIn(half_subtractor_1_carry_out), .CarryOut(full_subtractor_7_carryout), .o0(out_23));
  Half_Subtractor half_subtractor_1 (.a(a0), .b(b0), .o0(out_24), .Carry_Out(half_subtractor_1_carry_out));
endmodule

module Full_Subtractor (
  input  a,
  input  b,
  input  CarryIn,
  output CarryOut,
  output o0
);

  wire and_1_out, and_2_out, and_3_out, and_4_out, and_5_out, and_6_out, and_7_out, not_1_out, not_2_out,
       not_3_out, not_4_out, not_5_out, not_6_out, not_7_out, not_8_out;

  not not_1 (not_1_out, a);
  not not_2 (not_2_out, a);
  not not_3 (not_3_out, b);
  not not_4 (not_4_out, a);
  not not_5 (not_5_out, b);
  not not_6 (not_6_out, CarryIn);
  not not_7 (not_7_out, a);
  not not_8 (not_8_out, CarryIn);
  and and_1 (and_1_out, not_1_out, CarryIn);
  and and_2 (and_2_out, not_2_out, b);
  and and_3 (and_3_out, b, CarryIn);
  and and_4 (and_4_out, not_3_out, not_4_out, CarryIn);
  and and_5 (and_5_out, not_5_out, a, not_6_out);
  and and_6 (and_6_out, b, not_7_out, not_8_out);
  and and_7 (and_7_out, b, a, CarryIn);
  or or_1 (CarryOut, and_1_out, and_2_out, and_3_out);
  or or_2 (o0, and_4_out, and_5_out, and_6_out, and_7_out);
endmodule

module Half_Subtractor (
  input  a,
  input  b,
  output o0,
  output Carry_Out
);

  wire not_1_out;

  not not_1 (not_1_out, a);
  xor xor_1 (o0, a, b);
  and and_1 (Carry_Out, not_1_out, b);
endmodule

module bit_wise_AND (
  input  a7,
  input  a6,
  input  a5,
  input  a4,
  input  a3,
  input  a2,
  input  a1,
  input  a0,
  input  b7,
  input  b6,
  input  b5,
  input  b4,
  input  b3,
  input  b2,
  input  b1,
  input  b0,
  output out_17,
  output out_18,
  output out_19,
  output out_20,
  output out_21,
  output out_22,
  output out_23,
  output out_24
);

  and and_1 (out_17, b7, a7);
  and and_2 (out_18, b6, a6);
  and and_3 (out_19, b5, a5);
  and and_4 (out_21, b3, a3);
  and and_5 (out_20, b4, a4);
  and and_6 (out_22, b2, a2);
  and and_7 (out_23, b1, a1);
  and and_8 (out_24, b0, a0);
endmodule

// Control
module control (
  input  a7,
  input  a6,
  input  a5,
  input  a4,
  input  a3,
  input  a2,
  input  a1,
  input  a0,
  input  Control,
  output out_10,
  output out_11,
  output out_12,
  output out_13,
  output out_14,
  output out_15,
  output out_16,
  output out_17
);

  and and_1 (out_10, Control, a7);
  and and_2 (out_11, Control, a6);
  and and_3 (out_12, Control, a5);
  and and_4 (out_13, Control, a4);
  and and_5 (out_15, Control, a2);
  and and_6 (out_14, Control, a3);
  and and_7 (out_16, Control, a1);
  and and_8 (out_17, Control, a0);
endmodule

module _2bit_control (
  input  a,
  input  b,
  output x,
  output y,
  output z
);

  wire not_1_out, not_2_out;

  and and_1 (x, a, b);
  not not_1 (not_1_out, b);
  not not_2 (not_2_out, a);
  and and_2 (y, a, not_1_out);
  and and_3 (z, not_2_out, b);
endmodule

module Register_File (
  input  [7:0] WriteData,
  input  [1:0] WriteReg,
  input  [1:0] ReadReg1,
  input  [1:0] ReadReg2,
  input  RegWrite,
  input  Clock,
  output [7:0] ReadData1,
  output [7:0] ReadData2
);

  wire and_1_out, and_2_out, and_3_out, and_4_out, decoder_1_out0, decoder_1_out1, decoder_1_out2,
       decoder_1_out3;
  wire [7:0] multiplexer_1_out, multiplexer_2_out, multiplexer_3_out, multiplexer_4_out, register_1_q,
       register_2_q, register_3_q, register_4_q;

  Decoder #(.select(2), .enable("false")) decoder_1 (
    .out0(decoder_1_out0), .out1(decoder_1_out1), .out2(decoder_1_out2), .out3(decoder_1_out3), .sel(WriteReg));
  and and_1 (and_1_out, decoder_1_out0, RegWrite);
  and and_2 (and_2_out, decoder_1_out1, RegWrite);
  and and_3 (and_3_out, decoder_1_out2, RegWrite);
  and and_4 (and_4_out, decoder_1_out3, RegWrite);
  Multiplexer #(.width(8), .enable("false")) multiplexer_1 (
    .in0(register_1_q), .in1(WriteData), .out(multiplexer_1_out), .sel(and_1_out));
  Multiplexer #(.width(8), .enable("false")) multiplexer_2 (
    .in0(register_2_q), .in1(WriteData), .out(multiplexer_2_out), .sel(and_2_out));
  Multiplexer #(.width(8), .enable("false")) multiplexer_3 (
    .in0(register_3_q), .in1(WriteData), .out(multiplexer_3_out), .sel(and_3_out));
  Multiplexer #(.width(8), .enable("false")) multiplexer_4 (
    .in0(register_4_q), .in1(WriteData), .out(multiplexer_4_out), .sel(and_4_out));
  Register register_1 (.D(multiplexer_1_out), .Q(register_1_q), .clk(Clock));  // open: en, clr
  Register register_2 (.D(multiplexer_2_out), .Q(register_2_q), .clk(Clock));  // open: en, clr
  Register register_3 (.D(multiplexer_3_out), .Q(register_3_q), .clk(Clock));  // open: en, clr
  Register register_4 (.D(multiplexer_4_out), .Q(register_4_q), .clk(Clock));  // open: en, clr
  Multiplexer #(.select(2), .width(8), .enable("false")) multiplexer_5 (
    .in0(register_1_q), .in1(register_2_q), .in2(register_3_q), .in3(register_4_q), .out(ReadData1),
    .sel(ReadReg1));
  Multiplexer #(.select(2), .width(8), .enable("false")) multiplexer_6 (
    .in0(register_1_q), .in1(register_2_q), .in2(register_3_q), .in3(register_4_q), .out(ReadData2),
    .sel(ReadReg2));

  // Notes on the sheet:
  //   Register File 8x8-bits
endmodule

module Main (
  input  Reset,
  input  Load,
  output out_3,
  output out_4,
  output out_5,
  output out_6,
  output out_7,
  output out_8
);

  wire clock_1_out, or_1_out;
  wire [7:0] adder_1_out, and_1_out, register_1_q;
  wire [7:6] ram_1_data;

  or or_1 (or_1_out, Reset, and_1_out[3]);
  Register register_1 (.D(adder_1_out), .Q(register_1_q), .clk(clock_1_out), .clr(or_1_out));  // open: en
  assign and_1_out = register_1_q & 8'h8;  // AND_Gate and_1, 8 bits wide
  Adder adder_1 (.a(8'h1), .b(register_1_q), .out(adder_1_out));  // open: cin, cout
  Clock clock_1 (.out(clock_1_out));
  RAM ram_1 (
    .addr(register_1_q), .data({ram_1_data, out_3, out_6, out_4, out_7, out_5, out_8}), .sel(1'b1),
    .clk(clock_1_out), .ld(Load), .clr(Reset));
  Register_File register_file_1 ();  // open: WriteData, WriteReg, RegWrite, Clock, ReadData1, ReadReg1, ReadData2, ReadReg2
  Control_Circuit control_circuit_1 (.in_1(ram_1_data));  // open: MemRead, MemWrite, RegWrite, ALUcontrol, MemToReg, RegDst, AluSrc
  ALU alu_1 ();  // open: a7, b7, a6, b6, a5, b5, a4, b4, a3, b3, a2, b2, a1, b1, a0, b0, Bit_1, Bit_0
  RAM ram_2 ();  // open: addr, data, sel, clk, ld, clr
endmodule

module Control_Circuit (
  input  [1:0] in_1,
  output MemRead,
  output MemWrite,
  output RegWrite,
  output ALUcontrol,
  output MemToReg,
  output RegDst,
  output AluSrc
);

  wire Addi_out;

  and lw (MemRead, ~in_1[1], ~in_1[0]);  // AND_Gate
  and sw (MemWrite, ~in_1[1], in_1[0]);  // AND_Gate
  and Add (RegDst, in_1[1], ~in_1[0]);  // AND_Gate
  and Addi (Addi_out, in_1[0], in_1[1]);
  or or_1 (RegWrite, MemRead, RegDst, Addi_out);
  or or_2 (ALUcontrol, MemRead, MemWrite, RegDst, Addi_out);
  or or_3 (AluSrc, MemRead, MemWrite, Addi_out);

  assign MemToReg = MemRead;
endmodule
