// Logisim project ass5.circ as structural Verilog
module Control (
  input  [1:0] in_1,
  output MemRead,
  output MemWrite,
  output AluSrc,
  output RegWrite,
  output ALUcontrol,
  output MemToReg,
  output RegDst
);

  // AND_Gate lw has open pins: in0=in_1[1], in1=in_1[0], out=open
  // AND_Gate sw has open pins: in0=in_1[1], in1=in_1[0], out=open
  // AND_Gate Addi has open pins: in0=in_1[1], in1=in_1[0], out=open
  // AND_Gate Add has open pins: in0=in_1[0], in1=in_1[1], out=open
endmodule
